// Logisim project OneBit.circ as structural Verilog: 2 circuits, main circuit main
module main (
  input  in_1
);
endmodule

module Register (
  input  in_1,
  input  Read,
  input  Write
);

  wire and_1_out, nand_1_out, nand_2_out, nand_3_out, nand_4_out, not_1_out, pull_resistor_1_node;

  Pull_Resistor #(.pull(1)) pull_resistor_1 (.node(pull_resistor_1_node));
  and and_1 (and_1_out, pull_resistor_1_node, Read);
  and and_2 (pull_resistor_1_node, nand_4_out, Write);
  not not_1 (not_1_out, and_1_out);
  nand nand_1 (nand_1_out, not_1_out, in_1);
  nand nand_2 (nand_2_out, in_1, and_1_out);
  nand nand_3 (nand_3_out, nand_1_out, nand_4_out);
  nand nand_4 (nand_4_out, nand_3_out, nand_2_out);

  // Notes on the sheet:
  //   Clock
  //   Data
endmodule
